// Digital circuit 1x1 RAM.dig as structural Verilog
module _1x1_RAM (
  input  Write_Data,
  input  Write_Select,
  input  RS1,
  input  RS2,
  input  Clock,
  output RD1,
  output RD2
);

  wire d_ff_1_q, multiplexer_1_out;

  Multiplexer multiplexer_1 (.sel(Write_Select), .in_0(d_ff_1_q), .in_1(Write_Data), .out(multiplexer_1_out));
  D_FF d_ff_1 (.D(multiplexer_1_out), .C(Clock), .Q(d_ff_1_q));  // open: nQ
  and and_1 (RD1, RS1, d_ff_1_q);
  and and_2 (RD2, d_ff_1_q, RS2);
endmodule
