// Digital circuit 1x17 SRAM.dig as structural Verilog
module _1x17_SRAM (
  input  RS1,
  input  RS2,
  input  WS,
  input  [16:0] WD_16_0,
  input  Clock,
  output [16:0] RD1_16_0,
  output [16:0] RD2_16_0
);

  wire RD1_1;

  _1x1_RAM _1x1_ram_1 (
    .Write_Data(WD_16_0[0]), .Write_Select(WS), .RS1(RS1), .RS2(RS2), .Clock(Clock), .RD1(RD1_16_0[0]),
    .RD2(RD2_16_0[0]));
  _1x1_RAM _1x1_ram_2 (
    .Write_Data(WD_16_0[6]), .Write_Select(WS), .RS1(RS1), .RS2(RS2), .Clock(Clock), .RD1(RD1_16_0[6]),
    .RD2(RD2_16_0[6]));
  _1x1_RAM _1x1_ram_3 (
    .Write_Data(WD_16_0[12]), .Write_Select(WS), .RS1(RS1), .RS2(RS2), .Clock(Clock), .RD1(RD1_16_0[12]),
    .RD2(RD2_16_0[12]));
  _1x1_RAM _1x1_ram_4 (
    .Write_Data(WD_16_0[1]), .Write_Select(WS), .RS1(RS1), .RS2(RS2), .Clock(Clock), .RD1(RD1_1),
    .RD2(RD1_16_0[1]));
  _1x1_RAM _1x1_ram_5 (
    .Write_Data(WD_16_0[7]), .Write_Select(WS), .RS1(RS1), .RS2(RS2), .Clock(Clock), .RD1(RD1_16_0[7]),
    .RD2(RD2_16_0[7]));
  _1x1_RAM _1x1_ram_6 (
    .Write_Data(WD_16_0[13]), .Write_Select(WS), .RS1(RS1), .RS2(RS2), .Clock(Clock), .RD1(RD1_16_0[13]),
    .RD2(RD2_16_0[13]));
  _1x1_RAM _1x1_ram_7 (
    .Write_Data(WD_16_0[2]), .Write_Select(WS), .RS1(RS1), .RS2(RS2), .Clock(Clock), .RD1(RD1_16_0[2]),
    .RD2(RD2_16_0[2]));
  _1x1_RAM _1x1_ram_8 (
    .Write_Data(WD_16_0[8]), .Write_Select(WS), .RS1(RS1), .RS2(RS2), .Clock(Clock), .RD1(RD1_16_0[8]),
    .RD2(RD2_16_0[8]));
  _1x1_RAM _1x1_ram_9 (
    .Write_Data(WD_16_0[14]), .Write_Select(WS), .RS1(RS1), .RS2(RS2), .Clock(Clock), .RD1(RD1_16_0[14]),
    .RD2(RD2_16_0[14]));
  _1x1_RAM _1x1_ram_10 (
    .Write_Data(WD_16_0[3]), .Write_Select(WS), .RS1(RS1), .RS2(RS2), .Clock(Clock), .RD1(RD1_16_0[3]),
    .RD2(RD2_16_0[3]));
  _1x1_RAM _1x1_ram_11 (
    .Write_Data(WD_16_0[9]), .Write_Select(WS), .RS1(RS1), .RS2(RS2), .Clock(Clock), .RD1(RD1_16_0[9]),
    .RD2(RD2_16_0[9]));
  _1x1_RAM _1x1_ram_12 (
    .Write_Data(WD_16_0[15]), .Write_Select(WS), .RS1(RS1), .RS2(RS2), .Clock(Clock), .RD1(RD1_16_0[15]),
    .RD2(RD2_16_0[15]));
  _1x1_RAM _1x1_ram_13 (
    .Write_Data(WD_16_0[4]), .Write_Select(WS), .RS1(RS1), .RS2(RS2), .Clock(Clock), .RD1(RD1_16_0[4]),
    .RD2(RD2_16_0[4]));
  _1x1_RAM _1x1_ram_14 (
    .Write_Data(WD_16_0[10]), .Write_Select(WS), .RS1(RS1), .RS2(RS2), .Clock(Clock), .RD1(RD1_16_0[10]),
    .RD2(RD2_16_0[10]));
  _1x1_RAM _1x1_ram_15 (
    .Write_Data(WD_16_0[16]), .Write_Select(WS), .RS1(RS1), .RS2(RS2), .Clock(Clock), .RD1(RD1_16_0[16]),
    .RD2(RD2_16_0[16]));
  _1x1_RAM _1x1_ram_16 (
    .Write_Data(WD_16_0[5]), .Write_Select(WS), .RS1(RS1), .RS2(RS2), .Clock(Clock), .RD1(RD1_16_0[5]),
    .RD2(RD2_16_0[5]));
  _1x1_RAM _1x1_ram_17 (
    .Write_Data(WD_16_0[11]), .Write_Select(WS), .RS1(RS1), .RS2(RS2), .Clock(Clock), .RD1(RD1_16_0[11]),
    .RD2(RD2_16_0[11]));

  assign RD2_16_0[1] = RD1_16_0[1];

  // Other names for the same wires on the sheet: CLK = Clock; RD1_0 = RD1_16_0[0]; RD1_2 = RD1_16_0[2];
  //   RD1_3 = RD1_16_0[3]; RD1_4 = RD1_16_0[4]; RD1_5 = RD1_16_0[5]; RD1_6 = RD1_16_0[6]; RD1_7 = RD1_16_0[7];
  //   RD1_8 = RD1_16_0[8]; RD1_9 = RD1_16_0[9]; RD1_10 = RD1_16_0[10]; RD1_11 = RD1_16_0[11]; RD1_12 = RD1_16_0[12];
  //   RD1_13 = RD1_16_0[13]; RD1_14 = RD1_16_0[14]; RD1_15 = RD1_16_0[15]; RD1_16 = RD1_16_0[16]; RD2_0 = RD2_16_0[0];
  //   RD2_1 = RD1_16_0[1]; RD2_2 = RD2_16_0[2]; RD2_3 = RD2_16_0[3]; RD2_4 = RD2_16_0[4]; RD2_5 = RD2_16_0[5];
  //   RD2_6 = RD2_16_0[6]; RD2_7 = RD2_16_0[7]; RD2_8 = RD2_16_0[8]; RD2_9 = RD2_16_0[9]; RD2_10 = RD2_16_0[10];
  //   RD2_11 = RD2_16_0[11]; RD2_12 = RD2_16_0[12]; RD2_13 = RD2_16_0[13]; RD2_14 = RD2_16_0[14];
  //   RD2_15 = RD2_16_0[15]; RD2_16 = RD2_16_0[16]; WD0 = WD_16_0[0]; WD1 = WD_16_0[1]; WD2 = WD_16_0[2];
  //   WD3 = WD_16_0[3]; WD4 = WD_16_0[4]; WD5 = WD_16_0[5]; WD6 = WD_16_0[6]; WD7 = WD_16_0[7]; WD8 = WD_16_0[8];
  //   WD9 = WD_16_0[9]; WD10 = WD_16_0[10]; WD11 = WD_16_0[11]; WD12 = WD_16_0[12]; WD13 = WD_16_0[13];
  //   WD14 = WD_16_0[14]; WD15 = WD_16_0[15]; WD16 = WD_16_0[16]
endmodule
