// Digital circuit 6bitNOT.dig as structural Verilog
module _6bitNOT (
  input  [5:0] A_5_0,
  output [5:0] O_5_0
);

  not not_1 (O_5_0[0], A_5_0[0]);
  not not_2 (O_5_0[1], A_5_0[1]);
  not not_3 (O_5_0[2], A_5_0[2]);
  not not_4 (O_5_0[3], A_5_0[3]);
  not not_5 (O_5_0[4], A_5_0[4]);
  not not_6 (O_5_0[5], A_5_0[5]);
endmodule
