// Digital circuit 6bitROR.dig as structural Verilog
module _6bitROR (
  input  [5:0] A_5_0,
  input  [5:0] B_5_0,
  output [5:0] O_5_0
);

  Multiplexer #(.Selector_Bits(3)) multiplexer_1 (
    .sel(B_5_0[2:0]), .in_0(A_5_0[5]), .in_1(A_5_0[0]), .in_2(A_5_0[1]), .in_3(A_5_0[2]), .in_4(A_5_0[3]),
    .in_5(A_5_0[4]), .in_6(A_5_0[5]), .in_7(A_5_0[0]), .out(O_5_0[5]));
  Multiplexer #(.Selector_Bits(3)) multiplexer_2 (
    .sel(B_5_0[2:0]), .in_0(A_5_0[4]), .in_1(A_5_0[5]), .in_2(A_5_0[0]), .in_3(A_5_0[1]), .in_4(A_5_0[2]),
    .in_5(A_5_0[3]), .in_6(A_5_0[4]), .in_7(A_5_0[5]), .out(O_5_0[4]));
  Multiplexer #(.Selector_Bits(3)) multiplexer_3 (
    .sel(B_5_0[2:0]), .in_0(A_5_0[3]), .in_1(A_5_0[4]), .in_2(A_5_0[5]), .in_3(A_5_0[0]), .in_4(A_5_0[1]),
    .in_5(A_5_0[2]), .in_6(A_5_0[3]), .in_7(A_5_0[4]), .out(O_5_0[3]));
  Multiplexer #(.Selector_Bits(3)) multiplexer_4 (
    .sel(B_5_0[2:0]), .in_0(A_5_0[2]), .in_1(A_5_0[3]), .in_2(A_5_0[4]), .in_3(A_5_0[5]), .in_4(A_5_0[0]),
    .in_5(A_5_0[1]), .in_6(A_5_0[2]), .in_7(A_5_0[3]), .out(O_5_0[2]));
  Multiplexer #(.Selector_Bits(3)) multiplexer_5 (
    .sel(B_5_0[2:0]), .in_0(A_5_0[1]), .in_1(A_5_0[2]), .in_2(A_5_0[3]), .in_3(A_5_0[4]), .in_4(A_5_0[5]),
    .in_5(A_5_0[0]), .in_6(A_5_0[1]), .in_7(A_5_0[2]), .out(O_5_0[1]));
  Multiplexer #(.Selector_Bits(3)) multiplexer_6 (
    .sel(B_5_0[2:0]), .in_0(A_5_0[0]), .in_1(A_5_0[1]), .in_2(A_5_0[2]), .in_3(A_5_0[3]), .in_4(A_5_0[4]),
    .in_5(A_5_0[5]), .in_6(A_5_0[0]), .in_7(A_5_0[1]), .out(O_5_0[0]));
  // also tied to GND on the sheet: {B_5_0[3], B_5_0[4], B_5_0[5]}

  // Other names for the same wires on the sheet: Ao = A_5_0[0]; A1 = A_5_0[1]; A2 = A_5_0[2]; A3 = A_5_0[3];
  //   A4 = A_5_0[4]; A5 = A_5_0[5]; Bo = B_5_0[0]; Sel[2:0] = B_5_0[2:0]; B1 = B_5_0[1]; B2 = B_5_0[2]
endmodule
