// Digital circuit 6bit_register.dig as structural Verilog
module _6bit_register (
  input  [5:0] Din_5_0,
  input  Sel,
  input  Clock,
  output [5:0] Dout_5_0
);

  _1bit_register _1bit_register_1 (.Din(Din_5_0[0]), .Sel(Sel), .Clock(Clock), .Dout(Dout_5_0[0]));
  _1bit_register _1bit_register_2 (.Din(Din_5_0[1]), .Sel(Sel), .Clock(Clock), .Dout(Dout_5_0[1]));
  _1bit_register _1bit_register_3 (.Din(Din_5_0[2]), .Sel(Sel), .Clock(Clock), .Dout(Dout_5_0[2]));
  _1bit_register _1bit_register_4 (.Din(Din_5_0[3]), .Sel(Sel), .Clock(Clock), .Dout(Dout_5_0[3]));
  _1bit_register _1bit_register_5 (.Din(Din_5_0[4]), .Sel(Sel), .Clock(Clock), .Dout(Dout_5_0[4]));
  _1bit_register _1bit_register_6 (.Din(Din_5_0[5]), .Sel(Sel), .Clock(Clock), .Dout(Dout_5_0[5]));
endmodule
