// Digital circuit 6bitadder.dig as structural Verilog
module _6bitadder (
  input  [5:0] X_5_0,
  input  [5:0] Y_5_0,
  input  Cin,
  output [5:0] S_5_0,
  output Cout
);

  wire fa_2_cout, fa_3_cout, fa_4_cout, fa_5_cout, fa_6_cout, xor_1_out, xor_2_out, xor_3_out, xor_4_out,
       xor_5_out, xor_6_out;

  FA fa_1 (.Y(xor_1_out), .X(X_5_0[5]), .Cin(fa_2_cout), .S(S_5_0[5]), .Cout(Cout));
  xor xor_1 (xor_1_out, Cin, Y_5_0[5]);
  FA fa_2 (.Y(xor_2_out), .X(X_5_0[4]), .Cin(fa_3_cout), .S(S_5_0[4]), .Cout(fa_2_cout));
  xor xor_2 (xor_2_out, Cin, Y_5_0[4]);
  FA fa_3 (.Y(xor_3_out), .X(X_5_0[3]), .Cin(fa_4_cout), .S(S_5_0[3]), .Cout(fa_3_cout));
  xor xor_3 (xor_3_out, Cin, Y_5_0[3]);
  FA fa_4 (.Y(xor_4_out), .X(X_5_0[2]), .Cin(fa_5_cout), .S(S_5_0[2]), .Cout(fa_4_cout));
  xor xor_4 (xor_4_out, Cin, Y_5_0[2]);
  FA fa_5 (.Y(xor_5_out), .X(X_5_0[1]), .Cin(fa_6_cout), .S(S_5_0[1]), .Cout(fa_5_cout));
  xor xor_5 (xor_5_out, Cin, Y_5_0[1]);
  FA fa_6 (.Y(xor_6_out), .X(X_5_0[0]), .Cin(Cin), .S(S_5_0[0]), .Cout(fa_6_cout));
  xor xor_6 (xor_6_out, Cin, Y_5_0[0]);
endmodule
