// Digital circuit ALU_Circuit.dig as structural Verilog
module ALU_Circuit (
  input  [5:0] A_5_0,
  input  [5:0] B_5_0,
  input  [1:0] OP_1_0,
  output [5:0] R_5_0
);

  wire [5:0] _6bitadder_1_s_5_0, _6bitnot_1_o_5_0, _6bitror_1_o_5_0;

  _6bitadder _6bitadder_1 (.X_5_0(A_5_0), .Y_5_0(B_5_0), .Cin(1'b0), .S_5_0(_6bitadder_1_s_5_0));  // open: Cout
  _6bitNOT _6bitnot_1 (.A_5_0(A_5_0), .O_5_0(_6bitnot_1_o_5_0));
  _6bitROR _6bitror_1 (.A_5_0(A_5_0), .B_5_0(B_5_0), .O_5_0(_6bitror_1_o_5_0));
  Multiplexer #(.Selector_Bits(2), .Bits(6)) multiplexer_1 (
    .sel(OP_1_0), .in_0(_6bitadder_1_s_5_0), .in_1(_6bitnot_1_o_5_0), .in_2(_6bitror_1_o_5_0),
    .in_3({6{1'b0}}), .out(R_5_0));
endmodule
