// Digital circuit CPU.dig as structural Verilog
module CPU (
  input  [3:0] WA_3_0,
  input  WS,
  input  [16:0] WD_16_0,
  input  CLK,
  input  PC_EN,
  input  [3:0] RA2_3_0,
  input  CF,
  output [5:0] out_7,
  output [16:0] RD2,
  output [1:0] out_9,
  output [1:0] out_10,
  output [16:0] out_12
);

  wire CPU_CLK, Imm_sel, Jmp_sel, REG_en;
  wire [1:0] op;
  wire [3:0] _4bit_pc_adder_1_o_3_0, _4bit_program_counter_1_o_3_0, multiplexer_1_out;
  wire [5:0] _6bit_reg_set_1_a_5_0, _6bit_reg_set_1_b_5_0, multiplexer_2_out;

  Multiplexer #(.Bits(4)) multiplexer_1 (
    .sel(Jmp_sel), .in_0(_4bit_pc_adder_1_o_3_0), .in_1({out_9, out_10}), .out(multiplexer_1_out));
  _4bit_program_counter _4bit_program_counter_1 (
    .I_3_0(multiplexer_1_out), .CLK(CPU_CLK), .O_3_0(_4bit_program_counter_1_o_3_0));
  and and_1 (CPU_CLK, CLK, PC_EN);
  _4bit_PC_Adder _4bit_pc_adder_1 (.I_3_0(_4bit_program_counter_1_o_3_0), .O_3_0(_4bit_pc_adder_1_o_3_0));
  _9x17_SRAM _9x17_sram_1 (
    .RA1_3_0(_4bit_program_counter_1_o_3_0), .RA2_3_0(RA2_3_0), .WA_3_0(WA_3_0), .WS(WS), .WD_16_0(WD_16_0),
    .CLK(CLK), .RD1_16_0({out_12[16:13], out_9, out_10, out_12[8:0]}), .RD2_16_0(RD2));
  _6BIT_REG_SET _6bit_reg_set_1 (
    .RA_1_0(out_9), .RB_1_0(out_10), .WR_1_0(out_9), .WE(REG_en), .WRD_5_0(out_7), .Clock(CPU_CLK),
    .A_5_0(_6bit_reg_set_1_a_5_0), .B_5_0(_6bit_reg_set_1_b_5_0));
  CU cu_1 (.Opcode_3_0(out_12[16:13]), .CF(CF), .Op_1_0(op), .REG_EN(REG_en), .Imm_Sel(Imm_sel), .Jmp_Sel(Jmp_sel));
  Multiplexer #(.Bits(6)) multiplexer_2 (
    .sel(Imm_sel), .in_0(_6bit_reg_set_1_b_5_0), .in_1({out_10, out_12[8:5]}), .out(multiplexer_2_out));
  ALU_Circuit alu_circuit_1 (.A_5_0(_6bit_reg_set_1_a_5_0), .B_5_0(multiplexer_2_out), .OP_1_0(op), .R_5_0(out_7));

  assign out_12[12:9] = {out_9, out_10};

  // Other names for the same wires on the sheet: Don_t_care[8:0] = out_12[8:0]; Imm_val[5:0] = {out_10, out_12[8:5]};
  //   Jmp_addr[3:0] = {out_9, out_10}; R2[1:0] = out_10; R1[1:0] = out_9; opcode[3:0] = out_12[16:13];
  //   RA2[3:0] = RA2_3_0; Result[5:0] = out_7; WA[3:0] = WA_3_0; WD[16:0] = WD_16_0

  // Notes on the sheet:
  //   Register Mode(Type of operation[00]) = 2bit(Type of Operation)+2bit(ALU operation)+2bit(Register1)+2bit(Regsiter2)+9bit(Dont care)
  //   Immediate mode(Type of operation[01]) = 2bit(Type of Operation)+2bit(ALU operation)+2bit(Register1)+6bit(Imm value)+5bit(Dont care)
  //   Jump mode(Type of operation[10]) = 2bit(Type of Operation)+2bit(ALU operation)+2bit(Register1)+6bit(Jump value)+5bit(Dont care)
  //   Add(Op=00),NOT(01),ROR(OP=10)
  //   Add R1,5 -> 01 00 01 000101 00000
  //   Add R2,5 -> 01 00 10 000101 00000
  //   Add R1,R2 ->00 00 01 10 000000000
endmodule
